# Fritzing sketch dac_resistor_ladder (saved by Fritzing 0.9.3b)
breadboards: 1

parts:
  R2 = Resistor [tolerance=±5% resistance=10k package="2512 [SMD]"]
  R3 = Resistor [tolerance=±5% resistance=10k package="2512 [SMD]"]
  R4 = Resistor [tolerance=±5% resistance=10k package="2512 [SMD]"]
  R5 = Resistor [tolerance=±5% resistance=10k package="2512 [SMD]"]
  R6 = Resistor [tolerance=±5% resistance=10k package="2512 [SMD]"]
  R7 = Resistor [tolerance=±5% resistance=10k package="2512 [SMD]"]
  R8 = Resistor [tolerance=±5% resistance=10k package="2512 [SMD]"]
  R9 = Resistor [tolerance=±5% resistance=10k package="2512 [SMD]"]
  U1 = atmega328 [package=dip]
  VCC1 = Battery

nets:
  GND: R2.Pin_0, U1.GND
  N1: R2.Pin_1, R3.Pin_0, R6.Pin_1
  N2: R3.Pin_1, R4.Pin_0, R7.Pin_1
  N3: R4.Pin_1, R5.Pin_0, R8.Pin_1
  N4: R5.Pin_1, R9.Pin_1
  N5: R6.Pin_0, U1.D8
  N6: R7.Pin_0, U1.D9_(PWM)
  N7: R8.Pin_0, U1.D10_(PWM)
  N8: R9.Pin_0, U1.D11_(PWM)
  N9: U1.VCC, VCC1.-

notes:
  2R
  R
  PB0
  PB3
  PB2
  PB1
